// Logisim project brainfuck.circ as structural Verilog: 7 circuits, main circuit main
module main (
);

  wire and_3_out, and_4_out, and_7_out, clk, equals_8bit_1_out_3, equals_8bit_2_out_3, equals_8bit_3_out_3,
       equals_8bit_4_out_3, equals_8bit_5_out_3, equals_8bit_6_out_3, equals_8bit_7_out_3,
       equals_8bit_8_out_3, equals_8bit_11_out_3, equals_8bit_12_out_3, equals_8bit_13_out_3,
       equals_24bit_1_out_3, keyboard_1_avail, not_1_out, not_2_out, or_2_out, priority_encoder_1_p2,
       priority_encoder_1_p4, priority_encoder_1_p5, priority_encoder_2_p3, priority_encoder_2_p4;
  wire [1:0] equals_8bit_9_out_3, priority_encoder_1_p3, priority_encoder_2_p1, priority_encoder_3_p3;
  wire [6:0] keyboard_1_data;
  wire [7:0] decrement_8bit_1_out_2, increment_8bit_1_out_2, multiplexer_5_out, multiplexer_7_out,
       ram_2_data, rom_1_data;
  wire [23:0] brace_counter_q, Data_pointer_q, decrement_24bit_1_out_2, decrement_24bit_2_out_2,
       decrement_24bit_3_out_2, increment_24bit_1_out_2, increment_24bit_2_out_2, increment_24bit_3_out_2,
       increment_24bit_4_out_2, increment_24bit_5_out_2, multiplexer_1_out, multiplexer_2_out,
       multiplexer_3_out, multiplexer_4_out, multiplexer_6_out, Program_counter_q, ram_1_data,
       Stack_pointer_q;

  Decrement_24bit decrement_24bit_1 (.in_1(multiplexer_2_out), .out_2(decrement_24bit_1_out_2));
  Clock clock_1 (.out(clk));
  Register #(.width(24)) Stack_pointer (.D(multiplexer_1_out), .Q(Stack_pointer_q), .clk(clk));  // open: en, clr
  Multiplexer #(.width(24), .disabled(0), .enable("false")) multiplexer_1 (
    .in0(multiplexer_2_out), .in1(decrement_24bit_1_out_2), .out(multiplexer_1_out), .sel(and_3_out));
  Multiplexer #(.width(24), .disabled(0), .enable("false")) multiplexer_2 (
    .in0(Stack_pointer_q), .in1(increment_24bit_1_out_2), .out(multiplexer_2_out), .sel(and_4_out));
  Increment_24bit increment_24bit_1 (.in_1(Stack_pointer_q), .out_2(increment_24bit_1_out_2));
  Increment_24bit increment_24bit_2 (.in_1(Program_counter_q), .out_2(increment_24bit_2_out_2));
  Increment_24bit increment_24bit_3 (.in_1(Program_counter_q), .out_2(increment_24bit_3_out_2));
  RAM #(.addrWidth(24), .dataWidth(24), .bus("separate")) ram_1 (
    .addr(multiplexer_2_out), .din(increment_24bit_2_out_2), .data(ram_1_data), .str(and_4_out), .clk(clk));  // open: sel, ld, clr
  // Priority_Encoder #(.select(2), .disabled(0)) priority_encoder_1: pin names not known; wires that end beside it: 1'b1, priority_encoder_1_p2, priority_encoder_1_p3, priority_encoder_1_p4, priority_encoder_1_p5
  Multiplexer #(.select(2), .width(24), .disabled(0), .enable("false")) multiplexer_3 (
    .in0(increment_24bit_3_out_2), .in1(ram_1_data), .in2(increment_24bit_3_out_2), .in3(Program_counter_q),
    .out(multiplexer_3_out), .sel(priority_encoder_1_p3));
  and and_1 (priority_encoder_1_p2, equals_8bit_4_out_3, ~equals_8bit_6_out_3);  // AND_Gate
  and and_2 (priority_encoder_1_p4, equals_8bit_5_out_3, equals_8bit_6_out_3);
  and and_3 (and_3_out, equals_8bit_4_out_3, equals_8bit_6_out_3);
  and and_4 (and_4_out, equals_8bit_5_out_3, ~equals_8bit_6_out_3);  // AND_Gate
  or or_1 (priority_encoder_1_p5, equals_8bit_1_out_3, and_7_out);
  Register #(.width(24)) Program_counter (.D(multiplexer_3_out), .Q(Program_counter_q), .clk(clk));  // open: en, clr
  Register #(.width(24)) brace_counter (.D(multiplexer_4_out), .Q(brace_counter_q), .clk(clk));  // open: en, clr
  Increment_24bit increment_24bit_4 (.in_1(brace_counter_q), .out_2(increment_24bit_4_out_2));
  Decrement_24bit decrement_24bit_2 (.in_1(brace_counter_q), .out_2(decrement_24bit_2_out_2));
  Multiplexer #(.select(2), .width(24), .disabled(0), .enable("false")) multiplexer_4 (
    .in0(brace_counter_q), .in1(increment_24bit_4_out_2), .in2(decrement_24bit_2_out_2),
    .out(multiplexer_4_out), .sel(priority_encoder_2_p1));  // open: in3
  // Priority_Encoder #(.select(2), .disabled(0)) priority_encoder_2: pin names not known; wires that end beside it: priority_encoder_2_p1, 1'b1, priority_encoder_2_p3, priority_encoder_2_p4
  Equals_8bit equals_8bit_1 (.in_1(multiplexer_5_out), .in_2({8{1'b0}}), .out_3(equals_8bit_1_out_3));
  ROM #(.addrWidth(24)) rom_1 (.addr(Program_counter_q), .data(rom_1_data));  // open: sel
  Equals_24bit equals_24bit_1 (.in_1({24{1'b0}}), .in_2(brace_counter_q), .out_3(equals_24bit_1_out_3));
  not not_1 (not_1_out, equals_24bit_1_out_3);
  and and_5 (priority_encoder_2_p3, not_1_out, equals_8bit_2_out_3);
  Equals_8bit equals_8bit_2 (.in_1(8'h5d), .in_2(rom_1_data), .out_3(equals_8bit_2_out_3));
  Equals_8bit equals_8bit_3 (.in_1(8'h5b), .in_2(rom_1_data), .out_3(equals_8bit_3_out_3));
  and and_6 (priority_encoder_2_p4, equals_8bit_3_out_3, equals_8bit_6_out_3);
  Equals_8bit equals_8bit_4 (.in_1(8'h5d), .in_2(multiplexer_5_out), .out_3(equals_8bit_4_out_3));
  Equals_8bit equals_8bit_5 (.in_1(8'h5b), .in_2(multiplexer_5_out), .out_3(equals_8bit_5_out_3));
  Equals_8bit equals_8bit_6 (.in_1({8{1'b0}}), .in_2(ram_2_data), .out_3(equals_8bit_6_out_3));
  Equals_8bit equals_8bit_7 (.in_1(multiplexer_5_out), .in_2(8'h2e), .out_3(equals_8bit_7_out_3));
  Equals_8bit equals_8bit_8 (.in_1(multiplexer_5_out), .in_2(8'h2c), .out_3(equals_8bit_8_out_3));
  and and_7 (and_7_out, equals_8bit_8_out_3, not_2_out);
  Equals_8bit equals_8bit_9 (.in_1(8'h3e), .in_2(multiplexer_5_out), .out_3(equals_8bit_9_out_3[0]));
  Multiplexer #(.width(8), .disabled(0), .enable("false")) multiplexer_5 (
    .in0({8{1'b1}}), .in1(rom_1_data), .out(multiplexer_5_out), .sel(equals_24bit_1_out_3));
  Equals_8bit equals_8bit_10 (.in_1(8'h3c), .in_2(multiplexer_5_out), .out_3(equals_8bit_9_out_3[1]));
  TTY #(.rows(25), .cols(80)) tty_1 (.data(ram_2_data[6:0]), .clk(clk), .we(equals_8bit_7_out_3));  // open: clr
  Increment_24bit increment_24bit_5 (.in_1(Data_pointer_q), .out_2(increment_24bit_5_out_2));
  Multiplexer #(.select(2), .width(24), .disabled(0), .enable("false")) multiplexer_6 (
    .in0(Data_pointer_q), .in1(increment_24bit_5_out_2), .in2(decrement_24bit_3_out_2), .in3(Data_pointer_q),
    .out(multiplexer_6_out), .sel(equals_8bit_9_out_3));
  Decrement_24bit decrement_24bit_3 (.in_1(Data_pointer_q), .out_2(decrement_24bit_3_out_2));
  Equals_8bit equals_8bit_11 (.in_1(8'h2c), .in_2(multiplexer_5_out), .out_3(equals_8bit_11_out_3));
  Equals_8bit equals_8bit_12 (.in_1(8'h2d), .in_2(multiplexer_5_out), .out_3(equals_8bit_12_out_3));
  Equals_8bit equals_8bit_13 (.in_1(8'h2b), .in_2(multiplexer_5_out), .out_3(equals_8bit_13_out_3));
  Keyboard #(.buflen(128)) keyboard_1 (
    .clk(clk), .re(equals_8bit_8_out_3), .avail(keyboard_1_avail), .data(keyboard_1_data));  // open: clr
  Register #(.width(24)) Data_pointer (.D(multiplexer_6_out), .Q(Data_pointer_q), .clk(clk));  // open: en, clr
  // Priority_Encoder #(.select(2), .disabled(0)) priority_encoder_3: pin names not known; wires that end beside it: 1'b1, equals_8bit_13_out_3, priority_encoder_3_p3, equals_8bit_12_out_3, equals_8bit_11_out_3
  Increment_8bit increment_8bit_1 (.in_1(ram_2_data), .out_2(increment_8bit_1_out_2));
  Multiplexer #(.select(2), .width(8), .disabled(0), .enable("false")) multiplexer_7 (
    .in0(ram_2_data), .in1(increment_8bit_1_out_2), .in2(decrement_8bit_1_out_2),
    .in3({1'b0, keyboard_1_data}), .out(multiplexer_7_out), .sel(priority_encoder_3_p3));
  Decrement_8bit decrement_8bit_1 (.in_1(ram_2_data), .out_2(decrement_8bit_1_out_2));
  not not_2 (not_2_out, keyboard_1_avail);
  or or_2 (or_2_out, equals_8bit_11_out_3, equals_8bit_12_out_3, equals_8bit_13_out_3);
  RAM #(.addrWidth(24), .bus("separate")) ram_2 (
    .addr(Data_pointer_q), .din(multiplexer_7_out), .data(ram_2_data), .str(or_2_out), .clk(clk));  // open: sel, ld, clr

  // Notes on the sheet:
  //   PROGRAM MEMORY
  //   Halt when '00'
  //   contents of rom_1 (hex, n*v repeats v):
  //   3e 10*2b 3e 2b 3e 2b 5b 5b 5*2b 5b 3e 8*2b 3c 2d 5d 3e 2e 3c 6*2b 5b 3e 8*2d 3c 2d 5d 2b 3c 3c 3c 5d
  //   3e 2e 3e 3e 5b 5b 2d 5d 3c 5b 3e 2b 3c 2d 5d 3e 3e 5b 3c 3c 2b 3e 2b 3e 2d 5d 3c 5b 3e 2b 3c 2d 5b
  //   3e 2b 3c 2d 5b 3e 2b 3c 2d 5b 3e 2b 3c 2d 5b 3e 2b 3c 2d 5b 3e 2b 3c 2d 5b 3e 2b 3c 2d 5b 3e 2b 3c
  //   2d 5b 3e 2b 3c 2d 5b 3e 5b 2d 5d 3e 2b 3e 2b 3c 3c 3c 2d 5b 3e 2b 3c 2d 11*5d 2b 3e 3e 3e 5d 3c 3c
  //   3c 5d
endmodule

module Equals_8bit (
  input  [7:0] in_1,
  input  [7:0] in_2,
  output out_3
);

  wire [7:0] xnor_1_out;

  assign xnor_1_out = ~(in_1 ^ in_2);  // XNOR_Gate xnor_1, 8 bits wide
  and and_1 (out_3, xnor_1_out[0], xnor_1_out[1], xnor_1_out[2], xnor_1_out[3], xnor_1_out[4], xnor_1_out[5], xnor_1_out[6], xnor_1_out[7]);
endmodule

module Increment_24bit (
  input  [23:0] in_1,
  output [23:0] out_2
);

  Adder #(.width(24)) adder_1 (.a(in_1), .b(24'h1), .out(out_2), .cin(1'b0));  // open: cout
endmodule

module Decrement_24bit (
  input  [23:0] in_1,
  output [23:0] out_2
);

  Adder #(.width(24)) adder_1 (.a(in_1), .b({24{1'b1}}), .out(out_2), .cin(1'b0));  // open: cout
endmodule

module Increment_8bit (
  input  [7:0] in_1,
  output [7:0] out_2
);

  Adder adder_1 (.a(in_1), .b(8'h1), .out(out_2), .cin(1'b0));  // open: cout
endmodule

module Decrement_8bit (
  input  [7:0] in_1,
  output [7:0] out_2
);

  Adder adder_1 (.a(in_1), .b({8{1'b1}}), .out(out_2), .cin(1'b0));  // open: cout
endmodule

module Equals_24bit (
  input  [23:0] in_1,
  input  [23:0] in_2,
  output out_3
);

  wire and_1_out, and_2_out;
  wire [23:0] xnor_1_out;

  assign xnor_1_out = ~(in_1 ^ in_2);  // XNOR_Gate xnor_1, 24 bits wide
  and and_1 (and_1_out, xnor_1_out[0], xnor_1_out[1], xnor_1_out[2], xnor_1_out[3], xnor_1_out[4], xnor_1_out[5], xnor_1_out[6], xnor_1_out[7], xnor_1_out[8], xnor_1_out[9], xnor_1_out[10], xnor_1_out[11]);
  and and_2 (and_2_out, xnor_1_out[12], xnor_1_out[13], xnor_1_out[14], xnor_1_out[15], xnor_1_out[16], xnor_1_out[17], xnor_1_out[18], xnor_1_out[19], xnor_1_out[20], xnor_1_out[21], xnor_1_out[22], xnor_1_out[23]);
  and and_3 (out_3, and_1_out, and_2_out);
endmodule
